# Fritzing sketch BEACON-ESP32SuprMini (saved by Fritzing 0.9.6b)
breadboards: 1

parts:
  A1 = Esp32-c3 super mini [part_number="ESP32C3 Super mini"]
  Componente1 = Adafruit Si5351A Clock Generator [part_number="Adafruit #2045"]  # not connected
  OLED_I2C1 = OLED 128x64 I2C Monochrome Display [part_number=SSD1306]

nets:
  N1: A1.Pin_4, OLED_I2C1.SDA
  N2: A1.Pin_5, OLED_I2C1.SCK
  N3: A1.Pin_15, OLED_I2C1.GND
  N4: A1.Pin_16, OLED_I2C1.VDD

custom parts:
  Esp32-c3 super mini: ESP32-C3 Development Board ESP32 SuperMini Development Board ESP32 Development Board WiFi Bluetooth.
  Adafruit Si5351A Clock Generator: Never hunt around for another crystal again, with the Si5351A clock generator breakout from Adafruit! This chip has a precision 25MHz crystal reference and internal PLL and dividers so it can generate just about any frequency, from <8KHz up to 150+ MHz. The Si5351A clock generator is an I2C controller clock generator. It uses the onboard precision clock to drive multiple PLL's and clock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
